# Fritzing sketch ArduinoSpinner (saved by Fritzing 0.9.3b)
circuit board: 3.80131cm x 2.91121cm
breadboards: 1

parts:
  Part1 = Arduino Uno (Rev3)
  R2 = Resistor [tolerance=±5% resistance=220 package=THT]
  R3 = Resistor [tolerance=±5% resistance=220 package=THT]
  R5 = Resistor [tolerance=±5% resistance=220 package=THT]
  R6 = Resistor [tolerance=±5% resistance=220 package=THT]
  S1 = Pushbutton [package="[THT]"]
  R8 = Resistor [tolerance=±5% resistance=220 package=THT]
  R4 = Resistor [tolerance=±5% resistance=220 package=THT]
  R1 = Resistor [tolerance=±5% resistance=220 package=THT]
  R7 = Resistor [tolerance=±5% resistance=220 package=THT]
  7_Segment1 = 7 Segment Display

nets (from the breadboard view):
  N1: Part1.D8, R7.Pin_0
  N2: Part1.D9_PWM, R8.Pin_0
  N3: Part1.D10_PWM/SS, S1.Pin_3, S1.Pin_4
  N4: Part1.GND, S1.Pin_1, S1.Pin_2, 7_Segment1.common_anode
  N5: Part1.D2, R1.Pin_0
  N6: Part1.D3_PWM, R2.Pin_0
  N7: Part1.D4, R3.Pin_0
  N8: Part1.D5_PWM, R4.Pin_0
  N9: Part1.D6_PWM, R5.Pin_0
  N10: Part1.D7, R6.Pin_0
  N11: R2.Pin_1, 7_Segment1.Segment_G
  N12: R3.Pin_1, 7_Segment1.Segment_B
  N13: R5.Pin_1, 7_Segment1.Segment_D
  N14: R6.Pin_1, 7_Segment1.Segment_E
  N15: R8.Pin_1, 7_Segment1.Segment_A
  N16: R4.Pin_1, 7_Segment1.Segment_C
  N17: R1.Pin_1, 7_Segment1.Segment_DP
  N18: R7.Pin_1, 7_Segment1.Segment_F
